// Logisim project logi.circ as structural Verilog
module And16 (
  input  [15:0] a,
  input  [15:0] b,
  output [15:0] out
);

  assign out = a & b & b;  // AND_Gate and_1, 16 bits wide
endmodule

module AND (
  input  in,
  input  sel,
  output a
);

  wire nand_1_out;

  nand nand_1 (nand_1_out, in, sel, sel);
  not not_1 (a, nand_1_out);
endmodule

module Not16 (
  input  [15:0] in_1,
  input  [15:0] in_2,
  output [15:0] out_3,
  output [15:0] out_4
);

  not not_1 (out_3[0], in_1[0]);
  not not_2 (out_3[2], in_1[2]);
  not not_3 (out_3[4], in_1[4]);
  not not_4 (out_3[6], in_1[6]);
  not not_5 (out_3[8], in_1[8]);
  not not_6 (out_3[10], in_1[10]);
  not not_7 (out_3[12], in_1[12]);
  not not_8 (out_3[14], in_1[14]);
  assign out_4 = ~in_2;  // NOT_Gate not_9, 16 bits wide
  not not_10 (out_3[1], in_1[1]);
  not not_11 (out_3[3], in_1[3]);
  not not_12 (out_3[5], in_1[5]);
  not not_13 (out_3[7], in_1[7]);
  not not_14 (out_3[9], in_1[9]);
  not not_15 (out_3[11], in_1[11]);
  not not_16 (out_3[13], in_1[13]);
  not not_17 (out_3[15], in_1[15]);
endmodule

module Not (
  input  sel
);
endmodule

module Mux8Way16 (
  input  [15:0] in_1,
  input  [15:0] in_2,
  input  [15:0] in_3,
  input  [1:0] sel,
  input  [15:0] in_5,
  input  [15:0] in_6,
  input  [1:0] sel_2,
  input  [15:0] in_8,
  input  [15:0] in_9,
  input  [1:0] sel_3,
  input  [15:0] in_11,
  output [15:0] out
);

  wire [15:0] undriven, undriven_2;

  main main_1 ();
  main main_2 ();
  Multiplexer #(.select(2), .width(16)) multiplexer_1 (
    .in0(undriven), .in3(undriven_2), .out(out), .sel(sel_2));  // open: in1, in2, en
endmodule

module Dmux4Way (
  input  a,
  input  b,
  input  sel,
  input  in,
  input  sel_2,
  input  c,
  input  sel_3,
  input  d
);

  Demultiplexer demultiplexer_1 (.out0(sel), .out1(sel_2), .in(in), .en(sel_3));  // open: sel
  Demultiplexer demultiplexer_2 (.out0(a), .out1(b), .in(sel));  // open: sel, en
  Demultiplexer demultiplexer_3 (.out0(c), .out1(d), .in(sel_2));  // open: sel, en
endmodule

module Mux4way16 (
  input  [15:0] A,
  input  [15:0] B,
  input  [15:0] C,
  input  [15:0] A_2,
  input  [1:0] sel,
  output [15:0] out
);

  wire [15:0] multiplexer_1_out, multiplexer_2_out;

  Multiplexer #(.select(2), .width(16)) multiplexer_1 (
    .in1(A), .in3(B), .out(multiplexer_1_out), .sel(sel));  // open: in0, in2, en
  Multiplexer #(.select(2), .width(16)) multiplexer_2 (
    .in1(C), .in3(A_2), .out(multiplexer_2_out), .sel(sel));  // open: in0, in2, en
  Multiplexer #(.select(2), .width(16)) multiplexer_3 (
    .in1(multiplexer_1_out), .in3(multiplexer_2_out), .out(out), .sel(sel));  // open: in0, in2, en
endmodule

module Mux (
  input  sel,
  input  a,
  input  b,
  output out_4
);

  wire and_1_out, and_2_out, not_1_out;

  not not_1 (not_1_out, sel);
  and and_1 (and_1_out, sel, b);
  and and_2 (and_2_out, not_1_out, a);
  or or_1 (out_4, and_2_out, and_1_out);
endmodule

module Mux16 (
  input  [15:0] sel,
  input  [15:0] a,
  input  [15:0] b,
  output [15:0] out_4
);

  wire [15:0] and_1_out, and_2_out, not_1_out;

  assign not_1_out = ~sel;  // NOT_Gate not_1, 16 bits wide
  assign and_1_out = not_1_out & a;  // AND_Gate and_1, 16 bits wide
  assign and_2_out = sel & b;  // AND_Gate and_2, 16 bits wide
  assign out_4 = and_1_out | and_2_out;  // OR_Gate or_1, 16 bits wide
endmodule

module Or (
  input  A,
  input  B,
  output out
);

  wire undriven, undriven_2;

  Not not_1 (.sel(undriven));
  Not not_2 (.sel(undriven_2));
  Nand nand_1 (.inA(undriven), .inB(undriven_2), .out(out));
endmodule

module Nand (
  input  inA,
  input  inB,
  output out
);

  nand nand_1 (out, inA, inB);
endmodule

module or8way (
  input  in_1,
  input  in_2,
  input  in_3,
  input  in_4,
  input  in_5,
  input  in_6,
  input  in_7,
  input  in_8,
  output out_9
);

  wire or_1_out, or_2_out, or_3_out, or_4_out, or_5_out, or_6_out;

  or or_1 (or_1_out, in_1, in_2);
  or or_2 (or_2_out, in_3, in_4);
  or or_3 (or_3_out, in_5, in_6);
  or or_4 (or_4_out, in_7, in_8);
  or or_5 (or_5_out, or_1_out, or_2_out);
  or or_6 (or_6_out, or_3_out, or_4_out);
  or or_7 (out_9, or_5_out, or_6_out);
endmodule

module Or16 (
  input  [15:0] a,
  input  [15:0] b,
  output [15:0] out
);

  assign out = a | b;  // OR_Gate or_1, 16 bits wide
endmodule

module Xor (
  input  in_1,
  input  in_2,
  output out_3
);

  wire and_1_out, and_2_out, not_1_out, not_2_out;

  not not_1 (not_1_out, in_1);
  not not_2 (not_2_out, in_2);
  and and_1 (and_1_out, not_1_out, in_2);
  and and_2 (and_2_out, not_2_out, in_1);
  or or_1 (out_3, and_1_out, and_2_out);
endmodule
